// Digital circuit main.dig as structural Verilog
module main (
);

  // Processor processor_1: pin names not known
  Memory memory_1 ();  // open: Addr, Data_in, PC, C, str, Data_out, Instr
endmodule
